// Logisim project schematic.circ as structural Verilog: 1 circuit, main circuit main
module main (
  input  in_1,
  input  in_2,
  input  in_3,
  input  in_4,
  input  in_5,
  input  in_6,
  input  in_7,
  input  in_8,
  input  in_9,
  input  in_10,
  input  in_11,
  input  in_12,
  input  in_13,
  input  in_14,
  input  in_15,
  input  in_16,
  input  in_17,
  input  A,
  input  B,
  input  Cin,
  output S,
  output out_22,
  output out_23,
  output out_24,
  output out_25,
  output out_26,
  output out_27,
  output out_28,
  output out_29,
  output out_30,
  output out_31,
  output Cout
);

  wire adder_3_cout, adder_4_cout, adder_5_cout, adder_6_cout, adder_7_cout, adder_8_cout, and_1_out,
       and_2_out, B0, B1, B2, B3, B4, B5, B6, B7, COUT6, xor_10_out;

  Adder #(.width(1)) adder_1 (.a(in_1), .b(B7), .out(out_22), .cin(COUT6), .cout(out_30));
  Adder #(.width(1)) adder_2 (.a(in_2), .b(B6), .out(out_23), .cin(adder_3_cout), .cout(COUT6));
  xor xor_1 (B7, in_17, in_9);
  Adder #(.width(1)) adder_3 (.a(in_3), .b(B5), .out(out_24), .cin(adder_4_cout), .cout(adder_3_cout));
  xor xor_2 (B5, in_11, in_17);
  xor xor_3 (B6, in_10, in_17);
  xor xor_4 (B4, in_17, in_12);
  xor xor_5 (B3, in_13, in_17);
  Adder #(.width(1)) adder_4 (.a(in_4), .b(B4), .out(out_25), .cin(adder_5_cout), .cout(adder_4_cout));
  xor xor_6 (out_31, out_30, COUT6);
  xor xor_7 (B1, in_15, in_17);
  xor xor_8 (B2, in_14, in_17);
  Adder #(.width(1)) adder_5 (.a(in_5), .b(B3), .out(out_26), .cin(adder_6_cout), .cout(adder_5_cout));
  xor xor_9 (B0, in_16, in_17);
  Adder #(.width(1)) adder_6 (.a(in_6), .b(B2), .out(out_27), .cin(adder_7_cout), .cout(adder_6_cout));
  Adder #(.width(1)) adder_7 (.a(in_7), .b(B1), .out(out_28), .cin(adder_8_cout), .cout(adder_7_cout));
  xor xor_10 (xor_10_out, A, B);
  xor xor_11 (S, xor_10_out, Cin);
  and and_1 (and_1_out, Cin, xor_10_out);
  and and_2 (and_2_out, B, A);
  Adder #(.width(1)) adder_8 (.a(in_8), .b(B0), .out(out_29), .cin(in_17), .cout(adder_8_cout));
  or or_1 (Cout, and_1_out, and_2_out);

  // Other names for the same wires on the sheet: A0 = in_8; A1 = in_7; A2 = in_6; A3 = in_5; A4 = in_4; A5 = in_3;
  //   A6 = in_2; A7 = in_1; C_FLAG = out_30; OV_FLAG = out_31; S0 = out_29; S1 = out_28; S2 = out_27; S3 = out_26;
  //   S4 = out_25; S5 = out_24; S6 = out_23; S7 = out_22; T = in_17

  // Notes on the sheet:
  //   SALIDAS, RESULTADO (S), BANDER CARRY (C_FLAG), BANDERA OVERFLOW (OV_FLAG)
  //   FULLADDERS ENCADENADOS
  //   T=>1, B EN COMPLEMENTOS A1
  //   ENTRADAS, NUMEROS (A ,B) Y OPERACION (T)
  //   HAY OVERFLOW SI EL PENULTIMO 
  //   CARRY ES DIFERENTE AL ULTIMO
  //   SUMA=>0
  //   RESTA=>1
  //   CUANDO T=>1, SE LE SACA
  //   COMPLEMENTOS A2 AL #B
  //   ESTO CON EL FIN DE CAMBIAR
  //   EL SIGNO DEL NUMERO Y PODER
  //   USAR LA OPERACIÓN SUMA
  //   T Cin,CUANDO T=>1 SE AGREGA 1
  //   PARA PASAR B DE A1 A  A2
  //   FULLADDER CIRCUIT
endmodule
