// Logisim project Multiplicdor4_4.circ as structural Verilog: 1 circuit, main circuit main
module main (
  input  a3,
  input  a2,
  input  a1,
  input  a0,
  input  b0,
  input  in_6,
  input  b2,
  input  in_8,
  output out_9,
  output out_10,
  output out_11,
  output z4,
  output out_13,
  output out_14,
  output z1,
  output out_16
);

  wire multiplexer_10_out, multiplexer_12_out, multiplexer_13_out, multiplexer_14_out, multiplexer_16_out,
       multiplexer_19_out, multiplexer_20_out, multiplexer_22_out, not_1_out, not_2_out, not_3_out,
       not_4_out, not_5_out, not_6_out, not_7_out, not_8_out;
  wire [1:0] and_1_out, and_2_out, and_5_out, and_9_out, multiplexer_1_out, multiplexer_2_out,
       multiplexer_4_out, multiplexer_5_out, multiplexer_7_out, multiplexer_9_out, multiplexer_17_out,
       multiplexer_18_out;

  Multiplexer #(.select(2), .enable("false")) multiplexer_1 (
    .in0(1'b0), .in1(1'b0), .in2(1'b0), .in3(1'b1), .out(multiplexer_1_out[0]), .sel(and_2_out));
  Multiplexer #(.select(2), .enable("false")) multiplexer_2 (
    .in0(1'b0), .in1(multiplexer_10_out), .in2(multiplexer_10_out), .in3(1'b1), .out(multiplexer_2_out[0]),
    .sel(multiplexer_1_out));
  Multiplexer #(.select(2), .enable("false")) multiplexer_3 (
    .in0(1'b0), .in1(multiplexer_12_out), .in2(multiplexer_12_out), .in3(1'b1), .out(out_9),
    .sel(multiplexer_2_out));
  Multiplexer #(.select(2), .enable("false")) multiplexer_4 (
    .in0(1'b0), .in1(1'b1), .in2(1'b1), .in3(1'b0), .out(multiplexer_4_out[0]), .sel(and_2_out));
  not not_1 (not_1_out, multiplexer_10_out);
  Multiplexer #(.select(2), .enable("false")) multiplexer_5 (
    .in0(multiplexer_10_out), .in1(not_1_out), .in2(not_1_out), .in3(multiplexer_10_out),
    .out(multiplexer_5_out[0]), .sel(multiplexer_1_out));
  not not_2 (not_2_out, multiplexer_12_out);
  Multiplexer #(.select(2), .enable("false")) multiplexer_6 (
    .in0(multiplexer_12_out), .in1(not_2_out), .in2(not_2_out), .in3(multiplexer_12_out), .out(out_10),
    .sel(multiplexer_2_out));
  and and_1 (and_1_out[0], b0, a3);
  and and_2 (and_2_out[0], in_6, a3);
  and and_3 (multiplexer_1_out[1], b2, a3);
  and and_4 (multiplexer_2_out[1], in_8, a3);
  not not_3 (not_3_out, multiplexer_16_out);
  Multiplexer #(.select(2), .enable("false")) multiplexer_7 (
    .in0(multiplexer_16_out), .in1(not_3_out), .in2(not_3_out), .in3(multiplexer_16_out),
    .out(multiplexer_7_out[0]), .sel(and_1_out));
  Multiplexer #(.select(2), .enable("false")) multiplexer_8 (
    .in0(1'b0), .in1(multiplexer_16_out), .in2(multiplexer_16_out), .in3(1'b1), .out(and_2_out[1]),
    .sel(and_1_out));
  not not_4 (not_4_out, multiplexer_14_out);
  Multiplexer #(.select(2), .enable("false")) multiplexer_9 (
    .in0(multiplexer_14_out), .in1(not_4_out), .in2(not_4_out), .in3(multiplexer_14_out),
    .out(multiplexer_9_out[0]), .sel(multiplexer_4_out));
  Multiplexer #(.select(2), .enable("false")) multiplexer_10 (
    .in0(1'b0), .in1(multiplexer_14_out), .in2(multiplexer_14_out), .in3(1'b1), .out(multiplexer_10_out),
    .sel(multiplexer_4_out));
  not not_5 (not_5_out, multiplexer_13_out);
  Multiplexer #(.select(2), .enable("false")) multiplexer_11 (
    .in0(multiplexer_13_out), .in1(not_5_out), .in2(not_5_out), .in3(multiplexer_13_out), .out(out_11),
    .sel(multiplexer_5_out));
  Multiplexer #(.select(2), .enable("false")) multiplexer_12 (
    .in0(1'b0), .in1(multiplexer_13_out), .in2(multiplexer_13_out), .in3(1'b1), .out(multiplexer_12_out),
    .sel(multiplexer_5_out));
  and and_5 (and_5_out[0], b0, a2);
  and and_6 (and_1_out[1], in_6, a2);
  and and_7 (multiplexer_4_out[1], b2, a2);
  and and_8 (multiplexer_5_out[1], in_8, a2);
  Multiplexer #(.select(2), .enable("false")) multiplexer_13 (
    .in0(1'b0), .in1(multiplexer_19_out), .in2(multiplexer_19_out), .in3(1'b1), .out(multiplexer_13_out),
    .sel(multiplexer_9_out));
  Multiplexer #(.select(2), .enable("false")) multiplexer_14 (
    .in0(1'b0), .in1(multiplexer_20_out), .in2(multiplexer_20_out), .in3(1'b1), .out(multiplexer_14_out),
    .sel(multiplexer_7_out));
  not not_6 (not_6_out, multiplexer_19_out);
  Multiplexer #(.select(2), .enable("false")) multiplexer_15 (
    .in0(multiplexer_19_out), .in1(not_6_out), .in2(not_6_out), .in3(multiplexer_19_out), .out(z4),
    .sel(multiplexer_9_out));
  not not_7 (not_7_out, multiplexer_22_out);
  Multiplexer #(.select(2), .enable("false")) multiplexer_16 (
    .in0(1'b0), .in1(multiplexer_22_out), .in2(multiplexer_22_out), .in3(1'b1), .out(multiplexer_16_out),
    .sel(and_5_out));
  Multiplexer #(.select(2), .enable("false")) multiplexer_17 (
    .in0(multiplexer_22_out), .in1(not_7_out), .in2(not_7_out), .in3(multiplexer_22_out),
    .out(multiplexer_17_out[0]), .sel(and_5_out));
  not not_8 (not_8_out, multiplexer_20_out);
  Multiplexer #(.select(2), .enable("false")) multiplexer_18 (
    .in0(multiplexer_20_out), .in1(not_8_out), .in2(not_8_out), .in3(multiplexer_20_out),
    .out(multiplexer_18_out[0]), .sel(multiplexer_7_out));
  and and_9 (and_9_out[0], b0, a1);
  and and_10 (and_5_out[1], in_6, a1);
  and and_11 (multiplexer_7_out[1], b2, a1);
  and and_12 (multiplexer_9_out[1], in_8, a1);
  Multiplexer #(.select(2), .enable("false")) multiplexer_19 (
    .in0(1'b0), .in1(1'b0), .in2(1'b0), .in3(1'b1), .out(multiplexer_19_out), .sel(multiplexer_18_out));
  Multiplexer #(.select(2), .enable("false")) multiplexer_20 (
    .in0(1'b0), .in1(1'b0), .in2(1'b0), .in3(1'b1), .out(multiplexer_20_out), .sel(multiplexer_17_out));
  Multiplexer #(.select(2), .enable("false")) multiplexer_21 (
    .in0(1'b0), .in1(1'b1), .in2(1'b1), .in3(1'b0), .out(out_13), .sel(multiplexer_18_out));
  Multiplexer #(.select(2), .enable("false")) multiplexer_22 (
    .in0(1'b0), .in1(1'b0), .in2(1'b0), .in3(1'b1), .out(multiplexer_22_out), .sel(and_9_out));
  Multiplexer #(.select(2), .enable("false")) multiplexer_23 (
    .in0(1'b0), .in1(1'b1), .in2(1'b1), .in3(1'b0), .out(out_14), .sel(multiplexer_17_out));
  Multiplexer #(.select(2), .enable("false")) multiplexer_24 (
    .in0(1'b0), .in1(1'b1), .in2(1'b1), .in3(1'b0), .out(z1), .sel(and_9_out));
  and and_13 (out_16, b0, a0);
  and and_14 (and_9_out[1], in_6, a0);
  and and_15 (multiplexer_17_out[1], b2, a0);
  and and_16 (multiplexer_18_out[1], in_8, a0);

  // Notes on the sheet:
  //   z7
  //   z6
  //   z5
  //   z3
  //   z2
  //   z0
  //   b1
  //   b3
endmodule
