// Logisim project Adders.circ as structural Verilog: 1 circuit, main circuit main
module main (
  input  Cin,
  input  [1:0] S1__S0,
  input  [1:0] S1__S0_2,
  input  Cin_2,
  input  [1:0] S1__S0_3,
  input  [1:0] S1__S0_4,
  output z0,
  output z0_2,
  output z1,
  output z1_2,
  output z1_3,
  output z0_3,
  output out_13,
  output out_14
);

  wire not_1_out, not_2_out;

  not not_1 (not_1_out, Cin);
  Multiplexer #(.select(2), .enable("false")) multiplexer_1 (
    .in0(1'b0), .in1(Cin_2), .in2(Cin_2), .in3(1'b1), .out(z1_3), .sel(S1__S0_3));
  Multiplexer #(.select(2), .enable("false")) multiplexer_2 (
    .in0(Cin), .in1(not_1_out), .in2(not_1_out), .in3(Cin), .out(z0), .sel(S1__S0));
  Multiplexer #(.select(2), .enable("false")) multiplexer_3 (
    .in0(1'b0), .in1(Cin), .in2(Cin), .in3(1'b1), .out(z1), .sel(S1__S0));
  not not_2 (not_2_out, Cin_2);
  Multiplexer #(.select(2), .enable("false")) multiplexer_4 (
    .in0(Cin_2), .in1(not_2_out), .in2(not_2_out), .in3(Cin_2), .out(z0_3), .sel(S1__S0_3));
  Multiplexer #(.select(2), .enable("false")) multiplexer_5 (
    .in0(1'b0), .in1(1'b0), .in2(1'b0), .in3(1'b1), .out(out_13), .sel(S1__S0_4));
  Multiplexer #(.select(2), .enable("false")) multiplexer_6 (
    .in0(1'b0), .in1(1'b1), .in2(1'b1), .in3(1'b0), .out(z0_2), .sel(S1__S0_2));
  Multiplexer #(.select(2), .enable("false")) multiplexer_7 (
    .in0(1'b0), .in1(1'b0), .in2(1'b0), .in3(1'b1), .out(z1_2), .sel(S1__S0_2));
  Multiplexer #(.select(2), .enable("false")) multiplexer_8 (
    .in0(1'b0), .in1(1'b1), .in2(1'b1), .in3(1'b0), .out(out_14), .sel(S1__S0_4));

  // Notes on the sheet:
  //   Full adder
  //   Half adder
  //   z1
  //   z0
endmodule
