// Logisim project Multiplexor4_1.circ as structural Verilog: 1 circuit, main circuit main
module main (
  input  a0,
  input  a1,
  input  a2,
  input  a3,
  input  s1,
  input  s0,
  output z
);

  wire and_1_out, and_2_out, and_3_out, and_4_out, not_1_out, not_2_out;

  not not_1 (not_1_out, s1);
  not not_2 (not_2_out, s0);
  and and_1 (and_1_out, a0, not_1_out, not_2_out);
  and and_2 (and_2_out, a1, not_1_out, s0);
  and and_3 (and_3_out, a2, not_2_out, s1);
  and and_4 (and_4_out, a3, s0, s1);
  or or_1 (z, and_1_out, and_2_out, and_3_out, and_4_out);

  // Notes on the sheet:
  //   MUX 4:1
endmodule
