// Logisim project Multiplicdor4_4_A2.circ as structural Verilog: 1 circuit, main circuit main
module main (
  input  a3,
  input  a2,
  input  a1,
  input  a0,
  input  b0,
  input  in_6,
  input  b2,
  input  in_8,
  output out_9,
  output out_10,
  output out_11,
  output z4,
  output out_13,
  output out_14,
  output z1,
  output out_16
);

  wire multiplexer_9_out, multiplexer_11_out, multiplexer_14_out, multiplexer_15_out, multiplexer_16_out,
       multiplexer_18_out, multiplexer_21_out, multiplexer_22_out, multiplexer_24_out, not_1_out, not_2_out,
       not_3_out, not_4_out, not_5_out, not_6_out, not_7_out, not_8_out, not_9_out;
  wire [0:0] multiplexer_3_out, nand_2_out;
  wire [1:0] and_2_out, and_5_out, multiplexer_1_out, multiplexer_2_out, multiplexer_5_out,
       multiplexer_6_out, multiplexer_10_out, multiplexer_12_out, multiplexer_19_out, multiplexer_20_out,
       nand_1_out;

  Multiplexer #(.select(2), .enable("false")) multiplexer_1 (
    .in0(1'b0), .in1(multiplexer_9_out), .in2(multiplexer_9_out), .in3(1'b1), .out(multiplexer_1_out[0]),
    .sel({1'b1, nand_2_out[0]}));
  Multiplexer #(.select(2), .enable("false")) multiplexer_2 (
    .in0(1'b0), .in1(multiplexer_11_out), .in2(multiplexer_11_out), .in3(1'b1), .out(multiplexer_2_out[0]),
    .sel(multiplexer_1_out));
  Multiplexer #(.select(2), .enable("false")) multiplexer_3 (
    .in0(1'b0), .in1(multiplexer_14_out), .in2(multiplexer_14_out), .in3(1'b1), .out(multiplexer_3_out[0]),
    .sel(multiplexer_2_out));
  Multiplexer #(.select(2), .enable("false")) multiplexer_4 (
    .in0(1'b0), .in1(1'b0), .in2(1'b0), .in3(1'b1), .sel({1'b1, multiplexer_3_out[0]}));  // open: out
  not not_1 (not_1_out, multiplexer_9_out);
  Multiplexer #(.select(2), .enable("false")) multiplexer_5 (
    .in0(multiplexer_9_out), .in1(not_1_out), .in2(not_1_out), .in3(multiplexer_9_out),
    .out(multiplexer_5_out[0]), .sel({1'b1, nand_2_out[0]}));
  not not_2 (not_2_out, multiplexer_11_out);
  Multiplexer #(.select(2), .enable("false")) multiplexer_6 (
    .in0(multiplexer_11_out), .in1(not_2_out), .in2(not_2_out), .in3(multiplexer_11_out),
    .out(multiplexer_6_out[0]), .sel(multiplexer_1_out));
  not not_3 (not_3_out, multiplexer_14_out);
  Multiplexer #(.select(2), .enable("false")) multiplexer_7 (
    .in0(multiplexer_14_out), .in1(not_3_out), .in2(not_3_out), .in3(multiplexer_14_out), .out(out_10),
    .sel(multiplexer_2_out));
  Multiplexer #(.select(2), .enable("false")) multiplexer_8 (
    .in0(1'b0), .in1(1'b1), .in2(1'b1), .in3(1'b0), .out(out_9), .sel({1'b1, multiplexer_3_out[0]}));
  nand nand_1 (nand_1_out[0], b0, a3);
  nand nand_2 (nand_2_out[0], in_6, a3);
  nand nand_3 (multiplexer_1_out[1], b2, a3);
  and and_1 (multiplexer_2_out[1], in_8, a3);
  not not_4 (not_4_out, multiplexer_18_out);
  Multiplexer #(.select(2), .enable("false")) multiplexer_9 (
    .in0(1'b0), .in1(multiplexer_18_out), .in2(multiplexer_18_out), .in3(1'b1), .out(multiplexer_9_out),
    .sel(nand_1_out));
  Multiplexer #(.select(2), .enable("false")) multiplexer_10 (
    .in0(multiplexer_18_out), .in1(not_4_out), .in2(not_4_out), .in3(multiplexer_18_out),
    .out(multiplexer_10_out[0]), .sel(nand_1_out));
  not not_5 (not_5_out, multiplexer_16_out);
  Multiplexer #(.select(2), .enable("false")) multiplexer_11 (
    .in0(1'b0), .in1(multiplexer_16_out), .in2(multiplexer_16_out), .in3(1'b1), .out(multiplexer_11_out),
    .sel(multiplexer_5_out));
  Multiplexer #(.select(2), .enable("false")) multiplexer_12 (
    .in0(multiplexer_16_out), .in1(not_5_out), .in2(not_5_out), .in3(multiplexer_16_out),
    .out(multiplexer_12_out[0]), .sel(multiplexer_5_out));
  not not_6 (not_6_out, multiplexer_15_out);
  Multiplexer #(.select(2), .enable("false")) multiplexer_13 (
    .in0(multiplexer_15_out), .in1(not_6_out), .in2(not_6_out), .in3(multiplexer_15_out), .out(out_11),
    .sel(multiplexer_6_out));
  Multiplexer #(.select(2), .enable("false")) multiplexer_14 (
    .in0(1'b0), .in1(multiplexer_15_out), .in2(multiplexer_15_out), .in3(1'b1), .out(multiplexer_14_out),
    .sel(multiplexer_6_out));
  and and_2 (and_2_out[0], b0, a2);
  and and_3 (nand_1_out[1], in_6, a2);
  and and_4 (multiplexer_5_out[1], b2, a2);
  nand nand_4 (multiplexer_6_out[1], in_8, a2);
  Multiplexer #(.select(2), .enable("false")) multiplexer_15 (
    .in0(1'b0), .in1(multiplexer_21_out), .in2(multiplexer_21_out), .in3(1'b1), .out(multiplexer_15_out),
    .sel(multiplexer_12_out));
  Multiplexer #(.select(2), .enable("false")) multiplexer_16 (
    .in0(1'b0), .in1(multiplexer_22_out), .in2(multiplexer_22_out), .in3(1'b1), .out(multiplexer_16_out),
    .sel(multiplexer_10_out));
  not not_7 (not_7_out, multiplexer_21_out);
  Multiplexer #(.select(2), .enable("false")) multiplexer_17 (
    .in0(multiplexer_21_out), .in1(not_7_out), .in2(not_7_out), .in3(multiplexer_21_out), .out(z4),
    .sel(multiplexer_12_out));
  not not_8 (not_8_out, multiplexer_24_out);
  Multiplexer #(.select(2), .enable("false")) multiplexer_18 (
    .in0(1'b0), .in1(multiplexer_24_out), .in2(multiplexer_24_out), .in3(1'b1), .out(multiplexer_18_out),
    .sel(and_2_out));
  Multiplexer #(.select(2), .enable("false")) multiplexer_19 (
    .in0(multiplexer_24_out), .in1(not_8_out), .in2(not_8_out), .in3(multiplexer_24_out),
    .out(multiplexer_19_out[0]), .sel(and_2_out));
  not not_9 (not_9_out, multiplexer_22_out);
  Multiplexer #(.select(2), .enable("false")) multiplexer_20 (
    .in0(multiplexer_22_out), .in1(not_9_out), .in2(not_9_out), .in3(multiplexer_22_out),
    .out(multiplexer_20_out[0]), .sel(multiplexer_10_out));
  and and_5 (and_5_out[0], b0, a1);
  and and_6 (and_2_out[1], in_6, a1);
  and and_7 (multiplexer_10_out[1], b2, a1);
  nand nand_5 (multiplexer_12_out[1], in_8, a1);
  Multiplexer #(.select(2), .enable("false")) multiplexer_21 (
    .in0(1'b0), .in1(1'b0), .in2(1'b0), .in3(1'b1), .out(multiplexer_21_out), .sel(multiplexer_20_out));
  Multiplexer #(.select(2), .enable("false")) multiplexer_22 (
    .in0(1'b0), .in1(1'b0), .in2(1'b0), .in3(1'b1), .out(multiplexer_22_out), .sel(multiplexer_19_out));
  Multiplexer #(.select(2), .enable("false")) multiplexer_23 (
    .in0(1'b0), .in1(1'b1), .in2(1'b1), .in3(1'b0), .out(out_13), .sel(multiplexer_20_out));
  Multiplexer #(.select(2), .enable("false")) multiplexer_24 (
    .in0(1'b0), .in1(1'b0), .in2(1'b0), .in3(1'b1), .out(multiplexer_24_out), .sel(and_5_out));
  Multiplexer #(.select(2), .enable("false")) multiplexer_25 (
    .in0(1'b0), .in1(1'b1), .in2(1'b1), .in3(1'b0), .out(out_14), .sel(multiplexer_19_out));
  Multiplexer #(.select(2), .enable("false")) multiplexer_26 (
    .in0(1'b0), .in1(1'b1), .in2(1'b1), .in3(1'b0), .out(z1), .sel(and_5_out));
  and and_8 (out_16, b0, a0);
  and and_9 (and_5_out[1], in_6, a0);
  and and_10 (multiplexer_19_out[1], b2, a0);
  nand nand_6 (multiplexer_20_out[1], in_8, a0);

  // Notes on the sheet:
  //   z7
  //   z6
  //   z5
  //   MULTIPLICADOR A2
  //   z3
  //   z2
  //   z0
  //   b1
  //   b3
endmodule
