// Logisim project contador0_99.circ as structural Verilog: 1 circuit, main circuit main
module main (
);

  wire and_1_out, and_2_out, and_3_out, and_4_out, and_5_out, and_6_out, and_7_out, and_8_out, and_9_out,
       and_10_out, and_11_out, and_12_out, and_13_out, and_14_out, clock_1_out, clock_2_out, j_k_ff_1_q,
       j_k_ff_2_q, j_k_ff_3_q, j_k_ff_4_q, j_k_ff_5_q, j_k_ff_6_q, j_k_ff_7_q, j_k_ff_8_q, j_k_ff_9_q,
       j_k_ff_10_q, j_k_ff_11_q, j_k_ff_12_q, j_k_ff_13_q, j_k_ff_14_q, j_k_ff_15_q, j_k_ff_16_q;

  Clock clock_1 (.out(clock_1_out));
  J_K_Flip_Flop j_k_ff_1 (
    .J(1'b1), .clk(clock_1_out), .K(1'b1), .Q(j_k_ff_1_q), .en(1'b1), .reset(and_3_out));  // open: Qn, preset
  Clock clock_2 (.out(clock_2_out));
  and and_1 (and_1_out, j_k_ff_1_q, j_k_ff_2_q);
  J_K_Flip_Flop j_k_ff_2 (
    .J(j_k_ff_1_q), .clk(clock_1_out), .K(j_k_ff_1_q), .Q(j_k_ff_2_q), .en(1'b1), .reset(and_3_out));  // open: Qn, preset
  J_K_Flip_Flop j_k_ff_3 (
    .J(1'b1), .clk(clock_2_out), .K(1'b1), .Q(j_k_ff_3_q), .reset(and_8_out));  // open: Qn, preset, en
  and and_2 (and_2_out, j_k_ff_1_q, j_k_ff_5_q);
  and and_3 (and_3_out, j_k_ff_2_q, j_k_ff_5_q);
  and and_4 (and_4_out, and_1_out, j_k_ff_4_q);
  J_K_Flip_Flop j_k_ff_4 (
    .J(and_1_out), .clk(clock_1_out), .K(and_1_out), .Q(j_k_ff_4_q), .en(1'b1), .reset(and_3_out));  // open: Qn, preset
  J_K_Flip_Flop j_k_ff_5 (
    .J(and_4_out), .clk(clock_1_out), .K(and_4_out), .Q(j_k_ff_5_q), .en(1'b1), .reset(and_3_out));  // open: Qn, preset
  and and_5 (and_5_out, j_k_ff_3_q, j_k_ff_6_q);
  J_K_Flip_Flop j_k_ff_6 (
    .J(j_k_ff_3_q), .clk(clock_2_out), .K(j_k_ff_3_q), .Q(j_k_ff_6_q), .en(1'b1), .reset(and_8_out));  // open: Qn, preset
  J_K_Flip_Flop j_k_ff_7 (
    .J(1'b1), .clk(clock_1_out), .K(1'b1), .Q(j_k_ff_7_q), .en(and_2_out), .reset(and_10_out));  // open: Qn, preset
  J_K_Flip_Flop j_k_ff_8 (
    .J(and_5_out), .clk(clock_2_out), .K(and_5_out), .Q(j_k_ff_8_q), .en(1'b1), .reset(and_8_out));  // open: Qn, preset
  and and_6 (and_6_out, j_k_ff_7_q, j_k_ff_9_q);
  J_K_Flip_Flop j_k_ff_9 (
    .J(j_k_ff_7_q), .clk(clock_1_out), .K(j_k_ff_7_q), .Q(j_k_ff_9_q), .en(and_2_out), .reset(and_10_out));  // open: Qn, preset
  and and_7 (and_7_out, j_k_ff_3_q, j_k_ff_11_q);
  and and_8 (and_8_out, j_k_ff_6_q, j_k_ff_11_q);
  and and_9 (and_9_out, and_5_out, j_k_ff_8_q);
  and and_10 (and_10_out, j_k_ff_9_q, j_k_ff_12_q);
  and and_11 (and_11_out, and_6_out, j_k_ff_10_q);
  J_K_Flip_Flop j_k_ff_10 (
    .J(and_6_out), .clk(clock_1_out), .K(and_6_out), .Q(j_k_ff_10_q), .en(and_2_out), .reset(and_10_out));  // open: Qn, preset
  J_K_Flip_Flop j_k_ff_11 (
    .J(and_9_out), .clk(clock_2_out), .K(and_9_out), .Q(j_k_ff_11_q), .en(1'b1), .reset(and_8_out));  // open: Qn, preset
  J_K_Flip_Flop j_k_ff_12 (
    .J(and_11_out), .clk(clock_1_out), .K(and_11_out), .Q(j_k_ff_12_q), .en(and_2_out), .reset(and_10_out));  // open: Qn, preset
  J_K_Flip_Flop j_k_ff_13 (
    .J(1'b1), .clk(clock_2_out), .K(1'b1), .Q(j_k_ff_13_q), .reset(and_13_out));  // open: Qn, preset, en
  J_K_Flip_Flop j_k_ff_14 (
    .J(j_k_ff_13_q), .clk(clock_2_out), .K(j_k_ff_13_q), .Q(j_k_ff_14_q), .en(and_7_out), .reset(and_13_out));  // open: Qn, preset
  and and_12 (and_12_out, j_k_ff_13_q, j_k_ff_14_q);
  J_K_Flip_Flop j_k_ff_15 (
    .J(and_12_out), .clk(clock_2_out), .K(and_12_out), .Q(j_k_ff_15_q), .en(and_7_out), .reset(and_13_out));  // open: Qn, preset
  and and_13 (and_13_out, j_k_ff_14_q, j_k_ff_16_q);
  and and_14 (and_14_out, and_12_out, j_k_ff_15_q);
  J_K_Flip_Flop j_k_ff_16 (
    .J(and_14_out), .clk(clock_2_out), .K(and_14_out), .Q(j_k_ff_16_q), .en(and_7_out), .reset(and_13_out));  // open: Qn, preset
endmodule
