// Logisim project contador0_99.circ as structural Verilog: 1 circuit, main circuit main
module main (
  input  in_1,
  output out_2,
  output out_3,
  output out_4,
  output out_5,
  output out_6,
  output out_7,
  output out_8,
  output out_9
);

  wire and_4_out, and_5_out, and_6_out, and_7_out, and_9_out, and_10_out, and_11_out, and_12_out, and_13_out,
       and_14_out, and_15_out, and_16_out, and_17_out, and_18_out, CLK, EN, j_k_ff_1_qn, j_k_ff_2_qn,
       j_k_ff_3_qn, j_k_ff_4_qn, j_k_ff_5_qn, j_k_ff_6_qn, not_1_out, not_2_out, not_3_out, not_4_out,
       not_5_out, not_6_out, not_7_out, not_8_out, not_9_out, not_10_out, not_11_out, or_3_out, or_4_out,
       or_6_out, or_7_out, or_8_out, or_9_out, R, R2, RS, RS2, S, S2;

  Clock clock_1 (.out(CLK));
  not not_1 (not_1_out, out_7);
  not not_2 (not_2_out, out_9);
  and and_1 (R, out_6, not_2_out, not_1_out, out_8);
  and and_2 (S, out_6, out_7, out_8, out_9);
  or or_1 (RS, S, R);
  not not_3 (not_3_out, out_5);
  J_K_Flip_Flop j_k_ff_1 (.J(1'b1), .clk(CLK), .K(1'b1), .Q(out_9), .Qn(j_k_ff_1_qn), .preset(S), .en(1'b1), .reset(R));
  not not_4 (not_4_out, in_1);
  J_K_Flip_Flop j_k_ff_2 (.J(1'b1), .clk(CLK), .K(1'b1), .Q(out_5), .Qn(j_k_ff_2_qn), .preset(S2), .en(EN), .reset(R2));
  not not_5 (not_5_out, in_1);
  not not_6 (not_6_out, out_3);
  and and_3 (R2, out_2, not_3_out, not_6_out, out_4);
  and and_4 (and_4_out, in_1, out_9);
  and and_5 (and_5_out, j_k_ff_1_qn, not_4_out);
  and and_6 (and_6_out, in_1, out_5);
  and and_7 (and_7_out, j_k_ff_2_qn, not_5_out);
  and and_8 (S2, out_5, out_4, out_3, out_2);
  or or_2 (RS2, S2, R2);
  or or_3 (or_3_out, and_4_out, and_5_out);
  or or_4 (or_4_out, and_6_out, and_7_out);
  and and_9 (and_9_out, in_1, out_9, out_6);
  J_K_Flip_Flop j_k_ff_3 (
    .J(or_3_out), .clk(CLK), .K(or_3_out), .Q(out_8), .Qn(j_k_ff_3_qn), .en(1'b1), .reset(RS));  // open: preset
  J_K_Flip_Flop j_k_ff_4 (
    .J(or_4_out), .clk(CLK), .K(or_4_out), .Q(out_4), .Qn(j_k_ff_4_qn), .en(EN), .reset(RS2));  // open: preset
  not not_7 (not_7_out, out_9);
  not not_8 (not_8_out, out_8);
  not not_9 (not_9_out, in_1);
  and and_10 (and_10_out, not_9_out, not_7_out, not_8_out, not_11_out, not_10_out);
  or or_5 (EN, and_9_out, and_10_out);
  and and_11 (and_11_out, and_4_out, out_8);
  or or_6 (or_6_out, and_11_out, and_12_out);
  and and_12 (and_12_out, j_k_ff_3_qn, and_5_out);
  and and_13 (and_13_out, and_6_out, out_4);
  and and_14 (and_14_out, j_k_ff_4_qn, and_7_out);
  not not_10 (not_10_out, out_6);
  not not_11 (not_11_out, out_7);
  or or_7 (or_7_out, and_13_out, and_14_out);
  J_K_Flip_Flop j_k_ff_5 (
    .J(or_6_out), .clk(CLK), .K(or_6_out), .Q(out_7), .Qn(j_k_ff_5_qn), .en(1'b1), .reset(RS));  // open: preset
  J_K_Flip_Flop j_k_ff_6 (
    .J(or_7_out), .clk(CLK), .K(or_7_out), .Q(out_3), .Qn(j_k_ff_6_qn), .en(EN), .reset(RS2));  // open: preset
  and and_15 (and_15_out, and_11_out, out_7);
  and and_16 (and_16_out, j_k_ff_5_qn, and_12_out);
  and and_17 (and_17_out, and_13_out, out_3);
  and and_18 (and_18_out, j_k_ff_6_qn, and_14_out);
  or or_8 (or_8_out, and_15_out, and_16_out);
  or or_9 (or_9_out, and_17_out, and_18_out);
  J_K_Flip_Flop j_k_ff_7 (
    .J(or_8_out), .clk(CLK), .K(or_8_out), .Q(out_6), .preset(S), .en(1'b1), .reset(R));  // open: Qn
  J_K_Flip_Flop j_k_ff_8 (
    .J(or_9_out), .clk(CLK), .K(or_9_out), .Q(out_2), .preset(S2), .en(EN), .reset(R2));  // open: Qn

  // Other names for the same wires on the sheet: Q0 = out_9; Q1 = out_8; Q2 = out_7; Q3 = out_6; Q4 = out_5;
  //   Q5 = out_4; Q6 = out_3; Q7 = out_2; U_D = in_1
endmodule
