// Logisim project contador4bits.circ as structural Verilog: 1 circuit, main circuit main
module main (
  output out_1,
  output out_2,
  output out_3,
  output out_4
);

  wire and_1_out, and_2_out, clock_1_out;

  Clock clock_1 (.out(clock_1_out));
  J_K_Flip_Flop j_k_ff_1 (.J(1'b1), .clk(clock_1_out), .K(1'b1), .Q(out_4));  // open: Qn, preset, en, reset
  and and_1 (and_1_out, out_4, out_3);
  J_K_Flip_Flop j_k_ff_2 (.J(out_4), .clk(clock_1_out), .K(out_4), .Q(out_3));  // open: Qn, preset, en, reset
  and and_2 (and_2_out, and_1_out, out_2);
  J_K_Flip_Flop j_k_ff_3 (.J(and_1_out), .clk(clock_1_out), .K(and_1_out), .Q(out_2));  // open: Qn, preset, en, reset
  J_K_Flip_Flop j_k_ff_4 (.J(and_2_out), .clk(clock_1_out), .K(and_2_out), .Q(out_1));  // open: Qn, preset, en, reset

  // Other names for the same wires on the sheet: Q1 = out_4; Q2 = out_3; Q3 = out_2; Q4 = out_1

  // Notes on the sheet:
  //   4 BITS COUNTER
endmodule
