// Logisim project contadordecadas.circ as structural Verilog: 1 circuit, main circuit main
module main (
  output out_1,
  output out_2,
  output out_3,
  output out_4
);

  wire and_1_out, and_2_out, and_3_out, clock_1_out;

  Clock clock_1 (.out(clock_1_out));
  J_K_Flip_Flop j_k_ff_1 (
    .J(out_4), .clk(clock_1_out), .K(out_4), .Q(out_3), .reset(and_2_out));  // open: Qn, preset, en
  J_K_Flip_Flop j_k_ff_2 (.J(1'b1), .clk(clock_1_out), .K(1'b1), .Q(out_4), .reset(and_2_out));  // open: Qn, preset, en
  and and_1 (and_1_out, out_4, out_3);
  J_K_Flip_Flop j_k_ff_3 (
    .J(and_1_out), .clk(clock_1_out), .K(and_1_out), .Q(out_2), .reset(and_2_out));  // open: Qn, preset, en
  and and_2 (and_2_out, out_3, out_1);
  and and_3 (and_3_out, and_1_out, out_2);
  J_K_Flip_Flop j_k_ff_4 (
    .J(and_3_out), .clk(clock_1_out), .K(and_3_out), .Q(out_1), .reset(and_2_out));  // open: Qn, preset, en

  // Other names for the same wires on the sheet: Q1 = out_4; Q2 = out_3; Q3 = out_2; Q4 = out_1

  // Notes on the sheet:
  //   COUNTER 0-9
endmodule
