// Logisim project flipflopjk.circ as structural Verilog: 1 circuit, main circuit main
module main (
  input  PRESET,
  input  J,
  input  K,
  input  CLEAR,
  output out_5,
  output out_6
);

  wire clock_1_out, nand_1_out, nand_2_out, not_1_out, not_2_out;

  Clock clock_1 (.out(clock_1_out));
  nand nand_1 (nand_1_out, out_6, J, clock_1_out);
  nand nand_2 (nand_2_out, clock_1_out, K, out_5);
  not not_1 (not_1_out, PRESET);
  not not_2 (not_2_out, CLEAR);
  nand nand_3 (out_5, not_1_out, nand_1_out, out_6);
  nand nand_4 (out_6, out_5, nand_2_out, not_2_out);

  // Notes on the sheet:
  //   CLOCK
  //   FLIPFFLOP-JK
endmodule
