// Logisim project 3display7segmentos.circ as structural Verilog: 1 circuit, main circuit main
module main (
  input  in_1,
  input  in_2,
  input  in_3,
  input  in_4,
  input  in_5,
  input  in_6,
  input  in_7,
  input  in_8,
  input  in_9,
  input  in_10,
  input  in_11,
  input  in_12,
  input  in_13,
  input  in_14,
  input  in_15,
  input  in_16,
  input  in_17,
  input  in_18,
  input  in_19,
  input  in_20,
  input  in_21,
  output out_22,
  output out_23,
  output out_24,
  output out_25,
  output out_26,
  output out_27,
  output out_28,
  output out_29,
  output out_30
);

  wire A, a0, a1, a2, a3, A_prime, AND1, AND2, AND3, AND4, AND5, AND6, AND7, AND8, AND9, B, b0, b1, b2, b3,
       B_prime, C, c0, c1, c2, c3, C_prime, CLK, D, d0_t, d1_t, d2_t, d3_t, D_prime, e0, e1, e2, e3, f0, f1,
       f2, f3, g0, g1, g2, g3, not_5_out, not_6_out, not_7_out, not_8_out, not_9_out, not_10_out, not_11_out,
       not_12_out, not_13_out, not_14_out, not_15_out, not_16_out, not_17_out, not_18_out, not_19_out,
       not_20_out, not_21_out, not_22_out, not_23_out, not_24_out, not_25_out, not_26_out, not_27_out,
       not_28_out, not_29_out, not_30_out, not_31_out, not_32_out, not_33_out, not_34_out, not_35_out,
       not_36_out, OD, OD0, OD1, OD2, OD3, Q0_prime, Q1_prime;

  Clock clock_1 (.out(CLK));
  not not_1 (A_prime, A);
  not not_2 (B_prime, B);
  not not_3 (C_prime, C);
  not not_4 (D_prime, D);
  Multiplexer #(.select(2), .enable("false")) multiplexer_1 (
    .in0(in_16), .in1(in_12), .in2(in_8), .in3(in_4), .out(D), .sel({out_22, out_23}));
  J_K_Flip_Flop j_k_ff_1 (
    .J(1'b1), .clk(CLK), .K(1'b1), .Q(out_23), .Qn(Q0_prime), .en(1'b1), .reset(in_21));  // open: preset
  and and_1 (AND1, B, D);
  and and_2 (AND2, B_prime, D_prime);
  and and_3 (AND3, C, D);
  and and_4 (AND4, C_prime, D_prime);
  Multiplexer #(.select(2), .enable("false")) multiplexer_2 (
    .in0(in_15), .in1(in_11), .in2(in_7), .in3(in_3), .out(C), .sel({out_22, out_23}));
  and and_5 (AND5, C, D_prime);
  and and_6 (AND6, B_prime, C);
  and and_7 (AND8, B, C_prime);
  and and_8 (AND9, B, D_prime);
  J_K_Flip_Flop j_k_ff_2 (
    .J(out_23), .clk(CLK), .K(out_23), .Q(out_22), .Qn(Q1_prime), .en(1'b1));  // open: preset, reset
  and and_9 (AND7, B, C_prime, D);
  Multiplexer #(.select(2), .enable("false")) multiplexer_3 (
    .in0(in_14), .in1(in_10), .in2(in_4), .in3(in_2), .out(B), .sel({out_22, out_23}));
  Multiplexer #(.select(2), .enable("false")) multiplexer_4 (
    .in0(in_13), .in1(in_9), .in2(in_4), .in3(in_1), .out(A), .sel({out_22, out_23}));
  or or_1 (out_24, A, AND1, AND2, C);
  or or_2 (out_25, AND4, AND3, B_prime);
  or or_3 (out_26, B, D, C_prime);
  Multiplexer #(.select(2), .enable("false")) multiplexer_5 (
    .in0(in_20), .in1(in_19), .in2(in_18), .in3(in_17), .out(OD), .sel({out_22, out_23}));
  or or_4 (out_27, A, AND2, AND5, AND6, AND4);
  or or_5 (out_28, AND2, AND5);
  or or_6 (out_29, A, AND4, AND9, AND8);
  and and_10 (a3, out_24, out_23, out_22);
  and and_11 (b3, out_25, out_23, out_22);
  and and_12 (c3, out_26, out_23, out_22);
  and and_13 (d3_t, out_27, out_23, out_22);
  or or_7 (out_30, A, AND6, AND5, AND8);
  and and_14 (e3, out_28, out_23, out_22);
  and and_15 (f3, out_29, out_23, out_22);
  and and_16 (g3, out_30, out_23, out_22);
  and and_17 (OD3, OD, out_23, out_22);
  _7_Segment_Display u_7_segment_display_1 (.g(g3), .f(f3), .a(a3), .b(b3), .e(e3), .d(d3_t), .c(c3), .dp(OD3));
  not not_5 (not_5_out, out_23);
  not not_6 (not_6_out, out_22);
  not not_7 (not_7_out, out_23);
  not not_8 (not_8_out, out_22);
  not not_9 (not_9_out, out_23);
  not not_10 (not_10_out, out_22);
  not not_11 (not_11_out, out_23);
  not not_12 (not_12_out, out_22);
  not not_13 (not_13_out, out_22);
  not not_14 (not_14_out, out_22);
  not not_15 (not_15_out, out_22);
  not not_16 (not_16_out, out_22);
  not not_17 (not_17_out, out_23);
  not not_18 (not_18_out, out_23);
  not not_19 (not_19_out, out_23);
  not not_20 (not_20_out, out_23);
  _7_Segment_Display u_7_segment_display_2 (.g(g2), .f(f2), .a(a2), .b(b2), .e(e2), .d(d2_t), .c(c2), .dp(OD2));
  and and_18 (a0, out_24, not_5_out, not_6_out);
  and and_19 (b0, out_25, not_7_out, not_8_out);
  and and_20 (c0, out_26, not_9_out, not_10_out);
  and and_21 (d0_t, out_27, not_11_out, not_12_out);
  and and_22 (a1, out_24, out_23, not_13_out);
  and and_23 (b1, out_25, out_23, not_14_out);
  and and_24 (c1, out_26, out_23, not_15_out);
  and and_25 (d1_t, out_27, out_23, not_16_out);
  and and_26 (a2, out_24, not_17_out, out_22);
  and and_27 (b2, out_25, not_18_out, out_22);
  and and_28 (c2, out_26, not_19_out, out_22);
  and and_29 (d2_t, out_27, not_20_out, out_22);
  _7_Segment_Display u_7_segment_display_3 (.g(g1), .f(f1), .a(a1), .b(b1), .e(e1), .d(d1_t), .c(c1), .dp(OD1));
  not not_21 (not_21_out, out_23);
  not not_22 (not_22_out, out_22);
  not not_23 (not_23_out, out_23);
  not not_24 (not_24_out, out_22);
  not not_25 (not_25_out, out_23);
  not not_26 (not_26_out, out_22);
  not not_27 (not_27_out, out_23);
  not not_28 (not_28_out, out_22);
  not not_29 (not_29_out, out_22);
  not not_30 (not_30_out, out_22);
  not not_31 (not_31_out, out_22);
  not not_32 (not_32_out, out_22);
  not not_33 (not_33_out, out_23);
  not not_34 (not_34_out, out_23);
  not not_35 (not_35_out, out_23);
  not not_36 (not_36_out, out_23);
  _7_Segment_Display u_7_segment_display_4 (.g(g0), .f(f0), .a(a0), .b(b0), .e(e0), .d(d0_t), .c(c0), .dp(OD0));
  and and_30 (e0, out_28, not_21_out, not_22_out);
  and and_31 (f0, out_29, not_23_out, not_24_out);
  and and_32 (g0, out_30, not_25_out, not_26_out);
  and and_33 (OD0, OD, not_27_out, not_28_out);
  and and_34 (e1, out_28, out_23, not_29_out);
  and and_35 (f1, out_29, out_23, not_30_out);
  and and_36 (g1, out_30, out_23, not_31_out);
  and and_37 (OD1, OD, out_23, not_32_out);
  and and_38 (e2, out_28, not_33_out, out_22);
  and and_39 (f2, out_29, not_34_out, out_22);
  and and_40 (g2, out_30, not_35_out, out_22);
  and and_41 (OD2, OD, not_36_out, out_22);

  assign in_5 = in_4;
  assign in_6 = in_4;

  // Other names for the same wires on the sheet: Q0 = out_23; Q1 = out_22; a_t = out_24; b_t = out_25; c_t = out_26;
  //   D0 = in_20; D1 = in_19; D2 = in_18; D3 = in_17; d_t = out_27; e = out_28; f = out_29; g = out_30; I0 = in_16;
  //   I1 = in_15; I2 = in_14; I3 = in_13; I4 = in_12; I5 = in_11; I6 = in_10; I7 = in_9; I8 = in_8; I9 = in_7;
  //   I10 = in_4; I11 = in_4; I12 = in_4; I13 = in_3; I14 = in_2; I15 = in_1; O0 = A; O1 = B; O2 = C; O3 = D
endmodule
