// Logisim project maquinaEstados.circ as structural Verilog: 1 circuit, main circuit main
module main (
  input  in_1
);

  wire CLK, Q0, Q0_prime, Q1, Q1_prime, Q2, Q2_prime, Q3, Q3_prime;

  J_K_Flip_Flop j_k_ff_1 (
    .J(1'b1), .clk(CLK), .K(Q3_prime), .Q(Q0), .Qn(Q0_prime), .en(1'b1), .reset(in_1));  // open: preset
  J_K_Flip_Flop j_k_ff_2 (.J(1'b1), .clk(CLK), .K(Q0_prime), .Q(Q1), .Qn(Q1_prime), .en(1'b1));  // open: preset, reset
  J_K_Flip_Flop j_k_ff_3 (.J(1'b1), .clk(CLK), .K(Q1_prime), .Q(Q2), .Qn(Q2_prime), .en(1'b1));  // open: preset, reset
  J_K_Flip_Flop j_k_ff_4 (.J(1'b1), .clk(CLK), .K(Q2_prime), .Q(Q3), .Qn(Q3_prime), .en(1'b1));  // open: preset, reset
endmodule
