// Logisim project decoder7segmentos.circ as structural Verilog: 1 circuit, main circuit main
module main (
  input  in_1,
  input  in_2,
  input  in_3,
  input  in_4,
  output out_5,
  output out_6,
  output out_7,
  output out_8,
  output out_9,
  output out_10,
  output out_11
);

  wire A_prime, AND1, AND2, AND3, AND4, AND5, AND6, AND7, AND8, AND9, B_prime, C_prime, D_prime;

  not not_1 (A_prime, in_1);
  not not_2 (B_prime, in_2);
  not not_3 (C_prime, in_3);
  not not_4 (D_prime, in_4);
  and and_1 (AND1, in_2, in_4);
  and and_2 (AND2, B_prime, D_prime);
  and and_3 (AND3, in_3, in_4);
  and and_4 (AND4, C_prime, D_prime);
  and and_5 (AND5, in_3, D_prime);
  and and_6 (AND6, B_prime, in_3);
  and and_7 (AND7, in_2, C_prime, in_4);
  and and_8 (AND8, in_2, C_prime);
  and and_9 (AND9, in_2, D_prime);
  _7_Segment_Display u_7_segment_display_1 (
    .g(out_11), .f(out_10), .a(out_5), .b(out_6), .e(out_9), .d(out_8), .c(out_7));  // open: dp
  or or_1 (out_5, in_1, AND1, AND2, in_3);
  or or_2 (out_6, AND4, AND3, B_prime);
  or or_3 (out_7, in_2, in_4, C_prime);
  or or_4 (out_8, in_1, AND2, AND5, AND6, AND7);
  or or_5 (out_9, AND2, AND5);
  or or_6 (out_10, in_1, AND4, AND9, AND8);
  or or_7 (out_11, in_1, AND6, AND5, AND8);

  // Other names for the same wires on the sheet: A = in_1; a_t = out_5; B = in_2; b_t = out_6; C = in_3; c_t = out_7;
  //   D = in_4; d_t = out_8; e = out_9; f = out_10; g = out_11
endmodule
