// Logisim project Counter1_12.circ as structural Verilog: 1 circuit, main circuit main
module main (
  output Output,
  output out_2,
  output out_3,
  output out_4,
  output out_5,
  output out_6
);

  wire and_1_out, and_2_out, CLK, CLR1, CLR2, EN, Q0_prime, Q1_prime, Q2_prime, Q3_prime, Q4_prime, SET;

  Clock clock_1 (.out(CLK));
  J_K_Flip_Flop j_k_ff_1 (
    .J(1'b1), .clk(CLK), .K(1'b1), .Q(out_6), .Qn(Q0_prime), .preset(SET), .en(1'b1), .reset(Output));
  J_K_Flip_Flop j_k_ff_2 (
    .J(1'b1), .clk(CLK), .K(1'b1), .Q(out_2), .Qn(Q4_prime), .en(EN), .reset(CLR2));  // open: preset
  J_K_Flip_Flop j_k_ff_3 (
    .J(out_6), .clk(CLK), .K(out_6), .Q(out_5), .Qn(Q1_prime), .en(1'b1), .reset(Output));  // open: preset
  and and_1 (and_1_out, out_5, out_6);
  and and_2 (and_2_out, and_1_out, out_4);
  J_K_Flip_Flop j_k_ff_4 (
    .J(and_1_out), .clk(CLK), .K(and_1_out), .Q(out_4), .Qn(Q2_prime), .en(1'b1), .reset(Output));  // open: preset
  J_K_Flip_Flop j_k_ff_5 (
    .J(and_2_out), .clk(CLK), .K(and_2_out), .Q(out_3), .Qn(Q3_prime), .en(1'b1), .reset(Output));  // open: preset
  nor nor_1 (SET, out_6, out_5, out_4, out_3, out_2);
  and and_3 (CLR1, out_3, out_5);
  and and_4 (CLR2, out_6, out_5, out_2);
  or or_1 (Output, CLR1, CLR2);
  and and_5 (EN, out_3, out_6);

  // Other names for the same wires on the sheet: CLR = Output; Q0 = out_6; Q1 = out_5; Q2 = out_4; Q3 = out_3;
  //   Q4 = out_2

  // Notes on the sheet:
  //   Input
  //   4-Bit (Counter 1)
  //   1-Bit (Counter 2)
  //   Counter 1-12
  //   SET 0->1
  //   Asynchronus Clear in 10
  //   Asynchronus Clear in 13
  //   Asynchronus Clear First Counter
  //   Enable Counter 2 
endmodule
