// Logisim project FrequencyDivider.circ as structural Verilog: 1 circuit, main circuit main
module main (
  output Output,
  output out_2,
  output out_3,
  output out_4,
  output out_5,
  output out_6,
  output out_7,
  output out_8,
  output out_9
);

  wire and_1_out, and_2_out, and_3_out, and_4_out, CLK, En, Q0_prime, Q1_prime, Q2_prime, Q3_prime, Q4_prime,
       Q5_prime, Q6_prime, Q7_prime;

  Clock clock_1 (.out(CLK));
  J_K_Flip_Flop j_k_ff_1 (
    .J(1'b1), .clk(CLK), .K(1'b1), .Q(out_9), .Qn(Q0_prime), .en(1'b1), .reset(Output));  // open: preset
  J_K_Flip_Flop j_k_ff_2 (
    .J(1'b1), .clk(CLK), .K(1'b1), .Q(out_5), .Qn(Q4_prime), .en(En), .reset(Output));  // open: preset
  J_K_Flip_Flop j_k_ff_3 (
    .J(out_9), .clk(CLK), .K(out_9), .Q(out_8), .Qn(Q1_prime), .en(1'b1), .reset(Output));  // open: preset
  J_K_Flip_Flop j_k_ff_4 (
    .J(out_5), .clk(CLK), .K(out_5), .Q(out_4), .Qn(Q5_prime), .en(En), .reset(Output));  // open: preset
  and and_1 (and_1_out, out_8, out_9);
  and and_2 (and_2_out, out_4, out_5);
  and and_3 (and_3_out, and_1_out, out_7);
  J_K_Flip_Flop j_k_ff_5 (
    .J(and_1_out), .clk(CLK), .K(and_1_out), .Q(out_7), .Qn(Q2_prime), .en(1'b1), .reset(Output));  // open: preset
  and and_4 (and_4_out, and_2_out, out_3);
  J_K_Flip_Flop j_k_ff_6 (
    .J(and_2_out), .clk(CLK), .K(and_2_out), .Q(out_3), .Qn(Q6_prime), .en(En), .reset(Output));  // open: preset
  J_K_Flip_Flop j_k_ff_7 (
    .J(and_3_out), .clk(CLK), .K(and_3_out), .Q(out_6), .Qn(Q3_prime), .en(1'b1), .reset(Output));  // open: preset
  J_K_Flip_Flop j_k_ff_8 (
    .J(and_4_out), .clk(CLK), .K(and_4_out), .Q(out_2), .Qn(Q7_prime), .en(En), .reset(Output));  // open: preset
  and and_5 (En, out_6, out_7, out_8, out_9);
  and and_6 (Output, out_7, out_6, out_5, out_4);

  // Other names for the same wires on the sheet: CLR = Output; Q0 = out_9; Q1 = out_8; Q2 = out_7; Q3 = out_6;
  //   Q4 = out_5; Q5 = out_4; Q6 = out_3; Q7 = out_2

  // Notes on the sheet:
  //   Input
  //   4-Bit Counter 1
  //   4-Bit Counter 2
  //   Frequency Divider Mod 60, Counter 0-59
  //   Enable Counter 2
  //   Asynchronus Clear in 60
endmodule
