// Logisim project 4BitRegister.circ as structural Verilog: 1 circuit, main circuit main
module main (
  input  in_1,
  input  in_2,
  input  in_3,
  input  in_4,
  input  in_5,
  input  in_6,
  output out_7,
  output out_8,
  output out_9,
  output out_10
);

  wire CLK;

  D_Flip_Flop d_ff_1 (.clk(CLK), .D(in_1), .Q(out_7), .en(in_6), .reset(in_5));  // open: Qn, preset
  Clock clock_1 (.out(CLK));
  D_Flip_Flop d_ff_2 (.clk(CLK), .D(in_2), .Q(out_8), .en(in_6), .reset(in_5));  // open: Qn, preset
  D_Flip_Flop d_ff_3 (.clk(CLK), .D(in_3), .Q(out_9), .en(in_6), .reset(in_5));  // open: Qn, preset
  D_Flip_Flop d_ff_4 (.clk(CLK), .D(in_4), .Q(out_10), .en(in_6), .reset(in_5));  // open: Qn, preset

  // Other names for the same wires on the sheet: D0 = in_4; D1 = in_3; D2 = in_2; D3 = in_1; EN = in_6; Q0 = out_10;
  //   Q1 = out_9; Q2 = out_8; Q3 = out_7; Reset = in_5

  // Notes on the sheet:
  //   4 BIT Register
endmodule
